# Fritzing sketch EthernetGateway (saved by Fritzing 0.8.7b)

parts:
  Part1 = Arduino Ethernet Shield (Rev3)
  LCD1 = LCD screen  # not connected
  S1 = Pushbutton [package="[THT]"]
  R1 = Resistor [tolerance=±5% resistance=10k package=THT]
  Transceiver1 = nRF24L01 [package=module]

nets:
  N1: Part1.5V, S1.Pin_1
  GND: Part1.GND, R1.Pin_0, Transceiver1.GND
  N2: Part1.A0, Transceiver1.SCK
  N3: Part1.A1, Transceiver1.MOSI
  N4: Part1.A2, Transceiver1.MISO
  N5: Part1.D2, S1.Pin_3, S1.Pin_4
  N6: Part1.PWM_D5, Transceiver1.CE
  N7: Part1.PWM_D6, Transceiver1.CSN
  3V3: Part1.3V3, Transceiver1.VCC

custom parts:
  nRF24L01: nRF24L01 module
