# Fritzing sketch TempSensor (saved by Fritzing 0.8.7b)

parts:
  Transceiver1 = nRF24L01 [package=module]
  Nano1 = Arduino Nano v2.3
  R1 = Temperature Sensor (Thermistor) [thermistor_type=NTC package=THT]
  R2 = Resistor [tolerance=±5% resistance=10k package=THT]

nets:
  GND: Transceiver1.GND, Nano1.GND
  VCC: Transceiver1.VCC, Nano1.3V3
  N1: Transceiver1.CE, Nano1.D9
  N2: Transceiver1.CSN, Nano1.D10
  N3: Transceiver1.SCK, Nano1.D13
  N4: Transceiver1.MOSI, Nano1.D11
  N5: Transceiver1.MISO, Nano1.D12
  N6: Nano1.A1, R2.Pin_1
  N7: Nano1.+5V, R1.pin_1
  N8: Nano1.VIN, R2.Pin_0

custom parts:
  nRF24L01: nRF24L01 module
