# Fritzing sketch TempSensor_DHT (saved by Fritzing 0.8.7b)

parts:
  Transceiver1 = nRF24L01 [package=module]
  Nano1 = Arduino Nano v2.3
  RHT1 = Humidity and Temperature Sensor RHT03

nets:
  GND: Transceiver1.GND, Nano1.GND, RHT1.GND_1
  VCC: Transceiver1.VCC, Nano1.3V3
  N1: Transceiver1.CE, Nano1.D9
  N2: Transceiver1.CSN, Nano1.D10
  N3: Transceiver1.SCK, Nano1.D13
  N4: Transceiver1.MOSI, Nano1.D11
  N5: Transceiver1.MISO, Nano1.D12
  N6: Nano1.D2, RHT1.Vcc
  N7: Nano1.+5V, RHT1.Data-signal

custom parts:
  nRF24L01: nRF24L01 module
